# Fritzing sketch rpi-dht22-breadboard-big (saved by Fritzing 0.9.4)
circuit board: 5.06492cm x 4.22815cm
breadboards: 1

parts:
  DHT1 = DHT22 Humidity and Temperature Sensor
  Raspberry_Pi_1 = Raspberry Pi 3 [part_number=RPI-3-V1.2]
  R1 = Resistor [tolerance=±5% resistance=10k package=THT]

nets:
  VDD: DHT1.VDD, Raspberry_Pi_1.3v3, R1.Pin_1
  N1: DHT1.DATA, Raspberry_Pi_1.GIPO4, R1.Pin_0
  GND: DHT1.GND, Raspberry_Pi_1.GND
