# Fritzing sketch rpi-dht22 (saved by Fritzing 0.9.4)

parts:
  DHT1 = DHT22 Humidity and Temperature Sensor
  Raspberry_Pi_1 = Raspberry Pi 3 [part_number=RPI-3-V1.2]

nets:
  VDD: DHT1.VDD, Raspberry_Pi_1.3v3
  N1: DHT1.DATA, Raspberry_Pi_1.GIPO4
  GND: DHT1.GND, Raspberry_Pi_1.GND
